// Digital circuit PracticaSemaforo1.dig as structural Verilog
module PracticaSemaforo1 (
  input  Q0_2,
  input  Q1,
  input  Q2,
  output Q0,
  output Q1_2,
  output Q2_2
);

  wire and_1_out, and_2_out, not_1_out, not_2_out, not_3_out;

  not not_1 (not_1_out, Q0_2);
  not not_2 (not_2_out, Q1);
  not not_3 (not_3_out, Q2);
  and and_1 (and_1_out, not_1_out, not_2_out, not_3_out);
  and and_2 (and_2_out, not_1_out, not_2_out, Q2);
  and and_3 (Q1_2, not_3_out, not_2_out, Q0_2);
  and and_4 (Q2_2, not_3_out, Q1, Q0_2);
  or or_1 (Q0, and_1_out, and_2_out);
endmodule
