// Digital circuit SEMAFORO1.1.dig as structural Verilog
module SEMAFORO1_1 (
  input  C,
  input  Em,
  output RED,
  output YELLOW,
  output GREEN,
  output WHITE
);

  wire and_1_out, and_2_out, not_1_out, not_2_out, not_3_out, Q_2;

  not not_1 (not_1_out, Q_2);
  not not_2 (not_2_out, YELLOW);
  not not_3 (not_3_out, GREEN);
  and and_1 (and_1_out, YELLOW, not_1_out);
  and and_2 (and_2_out, not_2_out, not_1_out);
  D_FF D1 (.D(GREEN), .C(C), .Q(Q_2));  // open: nQ
  D_FF D2 (.D(and_1_out), .C(C), .Q(GREEN));  // open: nQ
  D_FF D3 (.D(and_2_out), .C(C), .Q(YELLOW));  // open: nQ
  and and_3 (RED, not_2_out, not_3_out);
  and and_4 (WHITE, C, Em);

  // Other names for the same wires on the sheet: Q_0 = YELLOW; Q_1 = GREEN
endmodule
