// Digital circuit Semv1.0.dig as structural Verilog
module Semv1_0 (
  input  C,
  output [2:0] cled
);

  wire and_1_out, and_2_out, not_1_out, not_2_out;

  not not_1 (not_1_out, cled[2]);
  not not_2 (not_2_out, cled[0]);
  and and_1 (and_1_out, cled[0], not_1_out);
  and and_2 (and_2_out, not_2_out, not_1_out);
  D_FF D1 (.D(cled[1]), .C(C), .Q(cled[2]));  // open: nQ
  D_FF D2 (.D(and_1_out), .C(C), .Q(cled[1]));  // open: nQ
  D_FF D3 (.D(and_2_out), .C(C), .Q(cled[0]));  // open: nQ

  // Other names for the same wires on the sheet: Q_0 = cled[0]; Q_1 = cled[1]; Q_2 = cled[2]
endmodule
